# Fritzing sketch chimes-circuit (saved by Fritzing 1.0.1rc)
breadboards: 1

parts:
  Part1 = Arduino Uno (Rev3) - ICSP
  Part2 = HC-SR501 Body Sensor Module [part_number=HC-SR501]
  Q1 = TIP120 Hi-Current Darlington Transistor [part_number=TIP120]
  L1 = Solenoid
  R1 = Resistor [tolerance=±5% resistance=1.5k package=THT]
  Q2 = TIP120 Hi-Current Darlington Transistor [part_number=TIP120]
  L2 = Solenoid
  R2 = Resistor [tolerance=±5% resistance=1.5k power=0.25W package=THT]
  Q3 = TIP120 Hi-Current Darlington Transistor [part_number=TIP120]
  L3 = Solenoid
  R3 = Resistor [tolerance=±5% resistance=1.5k power=0.25W package=THT]
  Q4 = TIP120 Hi-Current Darlington Transistor [part_number=TIP120]
  L4 = Solenoid
  R4 = Resistor [tolerance=±5% resistance=1.5k power=0.25W package=THT]
  Q5 = TIP120 Hi-Current Darlington Transistor [part_number=TIP120]
  L5 = Solenoid
  R5 = Resistor [tolerance=±5% resistance=1.5k power=0.25W package=THT]

nets:
  N1: Part1.D8, R1.Pin_0
  N2: Part1.D9_PWM, R2.Pin_0
  N3: Part1.D10_PWM/SS, R3.Pin_0
  N4: Part1.D11_PWM/MOSI, R4.Pin_0
  N5: Part1.D12/MISO, R5.Pin_0
  N6: Part1.D2, Part2.VCC
  N7: Part1.5V, Part2.OUT
  GND: Part1.GND, Part2.GND, Q1.EMITTER, Q3.EMITTER, Q4.EMITTER, Q5.EMITTER
  N8: Part1.VIN, L1.pin2, Q2.EMITTER, L2.pin2, L3.pin2, L4.pin2, L5.pin2
  N9: Q1.BASE, R1.Pin_1
  N10: Q1.COLLECTOR, L1.pin1
  N11: Q2.BASE, R2.Pin_1
  N12: Q2.COLLECTOR, L2.pin1
  N13: Q3.BASE, R3.Pin_1
  N14: Q3.COLLECTOR, L3.pin1
  N15: Q4.BASE, R4.Pin_1
  N16: Q4.COLLECTOR, L4.pin1
  N17: Q5.BASE, R5.Pin_1
  N18: Q5.COLLECTOR, L5.pin1

custom parts:
  HC-SR501 Body Sensor Module: Pyroelectric Infrared PIR Motion Sensor Detector Module
