# Fritzing sketch strangebox-circuit (saved by Fritzing 1.0.1rc)
breadboards: 1

parts:
  Part1 = Arduino Uno (Rev3) - ICSP
  U1 = WS2812 RGB LED matrix 1x8
  Q1 = TIP120 Hi-Current Darlington Transistor
  R4 = Resistor [tolerance=±5% resistance=1.5k power=0.25W package=THT]
  MP3-1 = Serial MP3 Player
  AMP1 = PAM8403 6W Stereo Amplifier
  SP1 = SPEAKER [package=pcb_mount_speaker]
  SP2 = SPEAKER [package=pcb_mount_speaker]

nets:
  5V: Part1.5V, U1.VCC, MP3-1.pin2, AMP1.POWER+
  N1: Part1.D8, U1.DIN
  N2: Part1.D10_PWM/SS, MP3-1.pin3
  N3: Part1.D11_PWM/MOSI, MP3-1.pin4
  N4: Part1.D7, Q1.BASE
  N5: U1.GND, R4.Pin_1, MP3-1.pin1, AMP1.POWER-
  N6: Q1.EMITTER, R4.Pin_0
  N7: AMP1.ROUT-, SP1.+
  N8: AMP1.ROUT+, SP1.-
  N9: AMP1.LOUT+, SP2.-
  N10: AMP1.LOUT-, SP2.+

notes:
  plug for servo testing
  plug for solenoid testing
  SparkFun AK9753 Human Precense Sensor

custom parts:
  WS2812 RGB LED matrix 1x8: WS2812 matrix 1x8
  Serial MP3 Player: The module is a kind of simple MP3 player device which is based on a high-quality MP3 audio chip---YX5300. It can support 8k Hz ~ 48k Hz sampling frequency MP3 and WAV file formats. There is a TF card socket on board, so you can plug the micro SD card that stores audio files. MCU can control the MP3 playback state by sending commands to the module via UART port, such as switch songs, change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
  PAM8403 6W Stereo Amplifier: PAM8403 6 Watt Stereo Amplifier
